// Logisim project adder.circ as structural Verilog: 2 circuits, main circuit main
module main (
  input  add_sub,
  input  in_2,
  input  [15:0] b,
  input  [15:0] a,
  output out_5,
  output [15:0] \output 
);

  wire n1bitadder_1_cout, n1bitadder_1_sum, n1bitadder_2_sum, n1bitadder_3_cout, n1bitadder_3_sum,
       n1bitadder_4_cout, n1bitadder_4_sum, n1bitadder_5_cout, n1bitadder_5_sum, n1bitadder_6_cout,
       n1bitadder_6_sum, n1bitadder_7_cout, n1bitadder_7_sum, n1bitadder_8_cout, n1bitadder_8_sum,
       n1bitadder_9_cout, n1bitadder_9_sum, n1bitadder_10_cout, n1bitadder_10_sum, n1bitadder_11_cout,
       n1bitadder_11_sum, n1bitadder_12_cout, n1bitadder_12_sum, n1bitadder_13_cout, n1bitadder_13_sum,
       n1bitadder_14_cout, n1bitadder_14_sum, n1bitadder_15_cout, n1bitadder_15_sum, n1bitadder_16_cout,
       n1bitadder_16_sum, not_1_out, not_2_out, not_3_out, not_4_out, not_5_out, not_6_out, not_7_out,
       not_8_out, not_9_out, not_10_out, not_11_out, not_12_out, not_13_out, not_14_out, not_15_out,
       not_16_out, xor_1_out, xor_2_out, xor_3_out, xor_4_out, xor_5_out, xor_6_out, xor_7_out, xor_8_out,
       xor_9_out, xor_10_out, xor_11_out, xor_12_out, xor_13_out, xor_14_out, xor_15_out, xor_16_out;

  Multiplexer multiplexer_1 (.in0(n1bitadder_1_sum), .in1(not_1_out), .out(\output [7]), .sel(add_sub));  // open: en
  not not_1 (not_1_out, n1bitadder_1_sum);
  _1bitadder u_1bitadder_1 (
    .a(xor_1_out), .b(b[7]), .Sum(n1bitadder_1_sum), .Cin(n1bitadder_3_cout), .Cout(n1bitadder_1_cout));
  xor xor_1 (xor_1_out, a[7], add_sub);
  Multiplexer multiplexer_2 (.in0(n1bitadder_2_sum), .in1(not_2_out), .out(\output [15]), .sel(add_sub));  // open: en
  not not_2 (not_2_out, n1bitadder_2_sum);
  _1bitadder u_1bitadder_2 (.a(xor_2_out), .b(b[15]), .Sum(n1bitadder_2_sum), .Cin(n1bitadder_4_cout), .Cout(out_5));
  xor xor_2 (xor_2_out, a[15], add_sub);
  Multiplexer multiplexer_3 (.in0(n1bitadder_3_sum), .in1(not_3_out), .out(\output [6]), .sel(add_sub));  // open: en
  not not_3 (not_3_out, n1bitadder_3_sum);
  _1bitadder u_1bitadder_3 (
    .a(xor_3_out), .b(b[6]), .Sum(n1bitadder_3_sum), .Cin(n1bitadder_5_cout), .Cout(n1bitadder_3_cout));
  xor xor_3 (xor_3_out, a[6], add_sub);
  Multiplexer multiplexer_4 (.in0(n1bitadder_4_sum), .in1(not_4_out), .out(\output [14]), .sel(add_sub));  // open: en
  not not_4 (not_4_out, n1bitadder_4_sum);
  _1bitadder u_1bitadder_4 (
    .a(xor_4_out), .b(b[14]), .Sum(n1bitadder_4_sum), .Cin(n1bitadder_6_cout), .Cout(n1bitadder_4_cout));
  xor xor_4 (xor_4_out, a[14], add_sub);
  Multiplexer multiplexer_5 (.in0(n1bitadder_5_sum), .in1(not_5_out), .out(\output [5]), .sel(add_sub));  // open: en
  not not_5 (not_5_out, n1bitadder_5_sum);
  _1bitadder u_1bitadder_5 (
    .a(xor_5_out), .b(b[5]), .Sum(n1bitadder_5_sum), .Cin(n1bitadder_7_cout), .Cout(n1bitadder_5_cout));
  xor xor_5 (xor_5_out, a[5], add_sub);
  Multiplexer multiplexer_6 (.in0(n1bitadder_6_sum), .in1(not_6_out), .out(\output [13]), .sel(add_sub));  // open: en
  not not_6 (not_6_out, n1bitadder_6_sum);
  _1bitadder u_1bitadder_6 (
    .a(xor_6_out), .b(b[13]), .Sum(n1bitadder_6_sum), .Cin(n1bitadder_8_cout), .Cout(n1bitadder_6_cout));
  xor xor_6 (xor_6_out, a[3], add_sub);
  Multiplexer multiplexer_7 (.in0(n1bitadder_7_sum), .in1(not_7_out), .out(\output [4]), .sel(add_sub));  // open: en
  not not_7 (not_7_out, n1bitadder_7_sum);
  _1bitadder u_1bitadder_7 (
    .a(xor_7_out), .b(b[4]), .Sum(n1bitadder_7_sum), .Cin(n1bitadder_9_cout), .Cout(n1bitadder_7_cout));
  xor xor_7 (xor_7_out, a[4], add_sub);
  Multiplexer multiplexer_8 (.in0(n1bitadder_8_sum), .in1(not_8_out), .out(\output [12]), .sel(add_sub));  // open: en
  not not_8 (not_8_out, n1bitadder_8_sum);
  _1bitadder u_1bitadder_8 (
    .a(xor_8_out), .b(b[12]), .Sum(n1bitadder_8_sum), .Cin(n1bitadder_10_cout), .Cout(n1bitadder_8_cout));
  xor xor_8 (xor_8_out, a[12], add_sub);
  Multiplexer multiplexer_9 (.in0(n1bitadder_9_sum), .in1(not_9_out), .out(\output [3]), .sel(add_sub));  // open: en
  Multiplexer multiplexer_10 (.in0(n1bitadder_11_sum), .in1(not_12_out), .out(\output [2]), .sel(add_sub));  // open: en
  not not_9 (not_9_out, n1bitadder_9_sum);
  _1bitadder u_1bitadder_9 (
    .a(xor_9_out), .b(b[3]), .Sum(n1bitadder_9_sum), .Cin(n1bitadder_11_cout), .Cout(n1bitadder_9_cout));
  xor xor_9 (xor_9_out, a[3], add_sub);
  Multiplexer multiplexer_11 (
    .in0(n1bitadder_10_sum), .in1(not_10_out), .out(\output [11]), .sel(add_sub));  // open: en
  not not_10 (not_10_out, n1bitadder_10_sum);
  _1bitadder u_1bitadder_10 (
    .a(xor_10_out), .b(b[11]), .Sum(n1bitadder_10_sum), .Cin(n1bitadder_12_cout), .Cout(n1bitadder_10_cout));
  xor xor_10 (xor_10_out, a[11], add_sub);
  Multiplexer multiplexer_12 (.in0(n1bitadder_13_sum), .in1(not_11_out), .out(\output [1]), .sel(add_sub));  // open: en
  not not_11 (not_11_out, n1bitadder_13_sum);
  not not_12 (not_12_out, n1bitadder_11_sum);
  _1bitadder u_1bitadder_11 (
    .a(xor_11_out), .b(b[2]), .Sum(n1bitadder_11_sum), .Cin(n1bitadder_13_cout), .Cout(n1bitadder_11_cout));
  xor xor_11 (xor_11_out, a[2], add_sub);
  Multiplexer multiplexer_13 (.in0(n1bitadder_14_sum), .in1(not_15_out), .out(\output [9]), .sel(add_sub));  // open: en
  Multiplexer multiplexer_14 (
    .in0(n1bitadder_12_sum), .in1(not_13_out), .out(\output [10]), .sel(add_sub));  // open: en
  not not_13 (not_13_out, n1bitadder_12_sum);
  _1bitadder u_1bitadder_12 (
    .a(xor_12_out), .b(b[10]), .Sum(n1bitadder_12_sum), .Cin(n1bitadder_14_cout), .Cout(n1bitadder_12_cout));
  xor xor_12 (xor_12_out, a[10], add_sub);
  Multiplexer multiplexer_15 (.in0(n1bitadder_15_sum), .in1(not_14_out), .out(\output [0]), .sel(add_sub));  // open: en
  not not_14 (not_14_out, n1bitadder_15_sum);
  _1bitadder u_1bitadder_13 (
    .a(xor_13_out), .b(b[1]), .Sum(n1bitadder_13_sum), .Cin(n1bitadder_15_cout), .Cout(n1bitadder_13_cout));
  xor xor_13 (xor_13_out, a[1], add_sub);
  Multiplexer multiplexer_16 (.in0(n1bitadder_16_sum), .in1(not_16_out), .out(\output [8]), .sel(add_sub));  // open: en
  not not_15 (not_15_out, n1bitadder_14_sum);
  _1bitadder u_1bitadder_14 (
    .a(xor_14_out), .b(b[9]), .Sum(n1bitadder_14_sum), .Cin(n1bitadder_16_cout), .Cout(n1bitadder_14_cout));
  xor xor_14 (xor_14_out, a[9], add_sub);
  _1bitadder u_1bitadder_15 (.a(xor_15_out), .b(b[0]), .Sum(n1bitadder_15_sum), .Cin(in_2), .Cout(n1bitadder_15_cout));
  xor xor_15 (xor_15_out, a[0], add_sub);
  not not_16 (not_16_out, n1bitadder_16_sum);
  _1bitadder u_1bitadder_16 (
    .a(xor_16_out), .b(b[8]), .Sum(n1bitadder_16_sum), .Cin(n1bitadder_1_cout), .Cout(n1bitadder_16_cout));
  xor xor_16 (xor_16_out, a[8], add_sub);

  // Other names for the same wires on the sheet: a_s = add_sub; s0 = \output [0]; s1 = \output [1]; s2 = \output [2];
  //   s3 = \output [3]; s4 = \output [4]; s5 = \output [5]; s6 = \output [6]; s7 = \output [7]; s8 = \output [8];
  //   s9 = \output [9]; s10 = \output [10]; s11 = \output [11]; s12 = \output [12]; s13 = \output [13];
  //   s14 = \output [14]; s15 = \output [15]
endmodule

module _1bitadder (
  input  Cin,
  input  a,
  input  b,
  output Sum,
  output Cout
);

  wire and_1_out, and_2_out, xor_1_out;

  and and_1 (and_1_out, b, a);
  xor xor_1 (xor_1_out, a, b);
  or or_1 (Cout, and_1_out, and_2_out);
  and and_2 (and_2_out, xor_1_out, Cin);
  xor xor_2 (Sum, Cin, xor_1_out);
endmodule
