// Logisim project circuit1a.circ as structural Verilog: 1 circuit, main circuit main
module main (
  input  A,
  input  B,
  input  C,
  output out
);

  wire and_1_out, and_2_out, not_1_out, not_2_out, or_1_out;

  and and_1 (and_1_out, A, B);
  and and_2 (and_2_out, B, not_1_out);
  not not_1 (not_1_out, C);
  not not_2 (not_2_out, and_1_out);
  or or_1 (or_1_out, and_2_out, C);
  or or_2 (out, not_2_out, or_1_out);
endmodule
