// Logisim project circuit1c.circ as structural Verilog: 1 circuit, main circuit main
module main (
  input  A,
  input  B,
  input  C,
  output out1,
  output out2
);

  wire and_1_out, and_3_out, not_1_out, not_2_out, not_3_out, or_1_out;

  not not_1 (not_1_out, A);
  not not_2 (not_2_out, C);
  not not_3 (not_3_out, B);
  and and_1 (and_1_out, not_1_out, B);
  and and_2 (out2, B, not_2_out);
  and and_3 (and_3_out, not_3_out, C);
  or or_1 (or_1_out, and_1_out, out2);
  or or_2 (out1, or_1_out, and_3_out);
endmodule
