// Logisim project fsm.circ as structural Verilog: 1 circuit, main circuit main
module main (
  input  in1,
  input  in2,
  output out
);

  wire and_1_out, and_2_out, and_3_out, and_4_out, and_5_out, and_6_out, clk, not_1_out, not_2_out,
       not_3_out, not_4_out, not_5_out, not_6_out, not_7_out, not_8_out, not_9_out, not_10_out, not_11_out,
       not_12_out, not_13_out, not_14_out, not_15_out, or_1_out, or_2_out, Q0, Q1;

  not not_1 (not_1_out, Q1);
  not not_2 (not_2_out, in1);
  not not_3 (not_3_out, Q1);
  not not_4 (not_4_out, in2);
  not not_5 (not_5_out, Q0);
  not not_6 (not_6_out, in1);
  not not_7 (not_7_out, Q0);
  not not_8 (not_8_out, in2);
  not not_9 (not_9_out, Q1);
  not not_10 (not_10_out, Q0);
  not not_11 (not_11_out, in1);
  not not_12 (not_12_out, Q1);
  not not_13 (not_13_out, Q0);
  not not_14 (not_14_out, in2);
  and and_1 (and_1_out, not_1_out, Q0, not_2_out, in2);
  and and_2 (and_2_out, not_3_out, Q0, in1, not_4_out);
  and and_3 (and_3_out, Q1, not_5_out, not_6_out, in2);
  and and_4 (and_4_out, Q1, not_7_out, in1, not_8_out);
  and and_5 (and_5_out, not_9_out, not_10_out, not_11_out, in2);
  and and_6 (and_6_out, not_12_out, not_13_out, in1, not_14_out);
  D_Flip_Flop d_ff_1 (.D(or_1_out), .clk(clk), .Q(Q1));  // open: Qn, preset, reset
  or or_1 (or_1_out, and_1_out, and_2_out, and_3_out, and_4_out);
  D_Flip_Flop d_ff_2 (.D(or_2_out), .clk(clk), .Q(Q0));  // open: Qn, preset, reset
  or or_2 (or_2_out, and_5_out, and_6_out);
  and and_7 (out, Q1, not_15_out);
  not not_15 (not_15_out, Q0);
  Clock clock_1 (.out(clk));
endmodule
