// Logisim project hw4.circ as structural Verilog: 11 circuits, main circuit cpu
// sub
module sixteenbitadder (
  input  sub,
  input  in_2,
  input  [15:0] B,
  input  [15:0] A,
  output ovf,
  output [15:0] result
);

  wire not_1_out, not_2_out, not_3_out, not_4_out, not_5_out, not_6_out, not_7_out, not_8_out, not_9_out,
       not_10_out, not_11_out, not_12_out, not_13_out, not_14_out, not_15_out, not_16_out,
       onebitadder_1_cout, onebitadder_1_sum, onebitadder_2_cout, onebitadder_2_sum, onebitadder_3_cout,
       onebitadder_3_sum, onebitadder_4_cout, onebitadder_4_sum, onebitadder_5_cout, onebitadder_5_sum,
       onebitadder_6_cout, onebitadder_6_sum, onebitadder_7_cout, onebitadder_7_sum, onebitadder_8_cout,
       onebitadder_8_sum, onebitadder_9_cout, onebitadder_9_sum, onebitadder_10_cout, onebitadder_10_sum,
       onebitadder_11_cout, onebitadder_11_sum, onebitadder_12_cout, onebitadder_12_sum, onebitadder_13_cout,
       onebitadder_13_sum, onebitadder_14_cout, onebitadder_14_sum, onebitadder_15_cout, onebitadder_15_sum,
       onebitadder_16_cout, onebitadder_16_sum, xor_1_out, xor_2_out, xor_4_out, xor_5_out, xor_6_out,
       xor_7_out, xor_8_out, xor_9_out, xor_10_out, xor_11_out, xor_12_out, xor_13_out, xor_14_out,
       xor_15_out, xor_16_out, xor_17_out;

  Multiplexer multiplexer_1 (.in0(onebitadder_1_sum), .in1(not_1_out), .out(result[7]), .sel(sub));  // open: en
  not not_1 (not_1_out, onebitadder_1_sum);
  onebitadder onebitadder_1 (
    .a(xor_1_out), .b(B[7]), .Sum(onebitadder_1_sum), .Cin(onebitadder_3_cout), .Cout(onebitadder_1_cout));
  xor xor_1 (xor_1_out, A[7], sub);
  Multiplexer multiplexer_2 (.in0(onebitadder_2_sum), .in1(not_2_out), .out(result[15]), .sel(sub));  // open: en
  not not_2 (not_2_out, onebitadder_2_sum);
  onebitadder onebitadder_2 (
    .a(xor_2_out), .b(B[15]), .Sum(onebitadder_2_sum), .Cin(onebitadder_4_cout), .Cout(onebitadder_2_cout));
  xor xor_2 (xor_2_out, A[15], sub);
  xor xor_3 (ovf, onebitadder_2_cout, onebitadder_4_cout);
  Multiplexer multiplexer_3 (.in0(onebitadder_3_sum), .in1(not_3_out), .out(result[6]), .sel(sub));  // open: en
  not not_3 (not_3_out, onebitadder_3_sum);
  onebitadder onebitadder_3 (
    .a(xor_4_out), .b(B[6]), .Sum(onebitadder_3_sum), .Cin(onebitadder_5_cout), .Cout(onebitadder_3_cout));
  xor xor_4 (xor_4_out, A[6], sub);
  Multiplexer multiplexer_4 (.in0(onebitadder_4_sum), .in1(not_4_out), .out(result[14]), .sel(sub));  // open: en
  not not_4 (not_4_out, onebitadder_4_sum);
  onebitadder onebitadder_4 (
    .a(xor_5_out), .b(B[14]), .Sum(onebitadder_4_sum), .Cin(onebitadder_6_cout), .Cout(onebitadder_4_cout));
  xor xor_5 (xor_5_out, A[14], sub);
  Multiplexer multiplexer_5 (.in0(onebitadder_5_sum), .in1(not_5_out), .out(result[5]), .sel(sub));  // open: en
  not not_5 (not_5_out, onebitadder_5_sum);
  onebitadder onebitadder_5 (
    .a(xor_6_out), .b(B[5]), .Sum(onebitadder_5_sum), .Cin(onebitadder_7_cout), .Cout(onebitadder_5_cout));
  xor xor_6 (xor_6_out, A[5], sub);
  Multiplexer multiplexer_6 (.in0(onebitadder_6_sum), .in1(not_6_out), .out(result[13]), .sel(sub));  // open: en
  not not_6 (not_6_out, onebitadder_6_sum);
  onebitadder onebitadder_6 (
    .a(xor_7_out), .b(B[13]), .Sum(onebitadder_6_sum), .Cin(onebitadder_8_cout), .Cout(onebitadder_6_cout));
  xor xor_7 (xor_7_out, A[13], sub);
  Multiplexer multiplexer_7 (.in0(onebitadder_7_sum), .in1(not_7_out), .out(result[4]), .sel(sub));  // open: en
  not not_7 (not_7_out, onebitadder_7_sum);
  onebitadder onebitadder_7 (
    .a(xor_8_out), .b(B[4]), .Sum(onebitadder_7_sum), .Cin(onebitadder_9_cout), .Cout(onebitadder_7_cout));
  xor xor_8 (xor_8_out, A[4], sub);
  Multiplexer multiplexer_8 (.in0(onebitadder_8_sum), .in1(not_8_out), .out(result[12]), .sel(sub));  // open: en
  not not_8 (not_8_out, onebitadder_8_sum);
  onebitadder onebitadder_8 (
    .a(xor_9_out), .b(B[12]), .Sum(onebitadder_8_sum), .Cin(onebitadder_10_cout), .Cout(onebitadder_8_cout));
  xor xor_9 (xor_9_out, A[12], sub);
  Multiplexer multiplexer_9 (.in0(onebitadder_11_sum), .in1(not_11_out), .out(result[2]), .sel(sub));  // open: en
  Multiplexer multiplexer_10 (.in0(onebitadder_9_sum), .in1(not_9_out), .out(result[3]), .sel(sub));  // open: en
  not not_9 (not_9_out, onebitadder_9_sum);
  onebitadder onebitadder_9 (
    .a(xor_10_out), .b(B[3]), .Sum(onebitadder_9_sum), .Cin(onebitadder_11_cout), .Cout(onebitadder_9_cout));
  xor xor_10 (xor_10_out, A[3], sub);
  Multiplexer multiplexer_11 (.in0(onebitadder_10_sum), .in1(not_10_out), .out(result[11]), .sel(sub));  // open: en
  not not_10 (not_10_out, onebitadder_10_sum);
  onebitadder onebitadder_10 (
    .a(xor_11_out), .b(B[11]), .Sum(onebitadder_10_sum), .Cin(onebitadder_12_cout), .Cout(onebitadder_10_cout));
  xor xor_11 (xor_11_out, A[11], sub);
  Multiplexer multiplexer_12 (.in0(onebitadder_13_sum), .in1(not_12_out), .out(result[1]), .sel(sub));  // open: en
  not not_11 (not_11_out, onebitadder_11_sum);
  not not_12 (not_12_out, onebitadder_13_sum);
  onebitadder onebitadder_11 (
    .a(xor_12_out), .b(B[2]), .Sum(onebitadder_11_sum), .Cin(onebitadder_13_cout), .Cout(onebitadder_11_cout));
  xor xor_12 (xor_12_out, A[2], sub);
  Multiplexer multiplexer_13 (.in0(onebitadder_12_sum), .in1(not_13_out), .out(result[10]), .sel(sub));  // open: en
  Multiplexer multiplexer_14 (.in0(onebitadder_14_sum), .in1(not_15_out), .out(result[9]), .sel(sub));  // open: en
  not not_13 (not_13_out, onebitadder_12_sum);
  onebitadder onebitadder_12 (
    .a(xor_13_out), .b(B[10]), .Sum(onebitadder_12_sum), .Cin(onebitadder_14_cout), .Cout(onebitadder_12_cout));
  xor xor_13 (xor_13_out, A[10], sub);
  Multiplexer multiplexer_15 (.in0(onebitadder_15_sum), .in1(not_14_out), .out(result[0]), .sel(sub));  // open: en
  not not_14 (not_14_out, onebitadder_15_sum);
  onebitadder onebitadder_13 (
    .a(xor_14_out), .b(B[1]), .Sum(onebitadder_13_sum), .Cin(onebitadder_15_cout), .Cout(onebitadder_13_cout));
  xor xor_14 (xor_14_out, A[1], sub);
  Multiplexer multiplexer_16 (.in0(onebitadder_16_sum), .in1(not_16_out), .out(result[8]), .sel(sub));  // open: en
  not not_15 (not_15_out, onebitadder_14_sum);
  onebitadder onebitadder_14 (
    .a(xor_15_out), .b(B[9]), .Sum(onebitadder_14_sum), .Cin(onebitadder_16_cout), .Cout(onebitadder_14_cout));
  xor xor_15 (xor_15_out, A[9], sub);
  onebitadder onebitadder_15 (
    .a(xor_16_out), .b(B[0]), .Sum(onebitadder_15_sum), .Cin(in_2), .Cout(onebitadder_15_cout));
  xor xor_16 (xor_16_out, A[0], sub);
  not not_16 (not_16_out, onebitadder_16_sum);
  onebitadder onebitadder_16 (
    .a(xor_17_out), .b(B[8]), .Sum(onebitadder_16_sum), .Cin(onebitadder_1_cout), .Cout(onebitadder_16_cout));
  xor xor_17 (xor_17_out, A[8], sub);

  // Other names for the same wires on the sheet: s0 = result[0]; s1 = result[1]; s2 = result[2]; s3 = result[3];
  //   s4 = result[4]; s5 = result[5]; s6 = result[6]; s7 = result[7]; s8 = result[8]; s9 = result[9];
  //   s10 = result[10]; s11 = result[11]; s12 = result[12]; s13 = result[13]; s14 = result[14]; s15 = result[15]
endmodule

module onebitadder (
  input  Cin,
  input  a,
  input  b,
  output Sum,
  output Cout
);

  wire and_1_out, and_2_out, xor_1_out;

  and and_1 (and_1_out, b, a);
  xor xor_1 (xor_1_out, a, b);
  or or_1 (Cout, and_1_out, and_2_out);
  and and_2 (and_2_out, xor_1_out, Cin);
  xor xor_2 (Sum, Cin, xor_1_out);
endmodule

module cpu (
  input  reset
);

  wire ALUinB, and_1_out, Blt, BR, clk, clock_1_out, DMwe, IRe, J, JAL, keyboard_1_avail,
       memory_latch_1_oe_latched, memory_latch_1_we_latched, multiplexer_3_out, neg, not_1_out, not_2_out,
       not_3_out, not_5_out, not_6_out, not_7_out, not_8_out, not_9_out, OWre, Rdst, RShft, Rwd, Rwe, Shft,
       sub, zero;
  wire [1:0] ALUop;
  wire [2:0] amt, bitselector_4_out, bitselector_5_out, bitselector_6_out, multiplexer_7_out,
       multiplexer_8_out;
  wire [3:0] bitselector_3_out;
  wire [5:0] bitselector_7_out;
  wire [6:0] ascii, keyboard_1_data;
  wire [11:0] bitselector_2_out;
  wire [15:0] alu_1_result, alu_2_result, alu_3_result, bit_extender_1_out, immd, jaddr, keyin,
       lshifter_1_result, memory_latch_1_address_latched, memory_latch_1_data_in_latched, multiplexer_1_out,
       multiplexer_2_out, multiplexer_5_out, multiplexer_6_out, multiplexer_9_out, multiplexer_11_out,
       multiplexer_12_out, ram_1_dout, reg_1_result, registerfile_1_rs1val, rshifter_1_result, rt, shiftOut,
       undriven;

  TTY #(.rows(13), .cols(80), .trigger("falling")) tty_1 (.data(ascii), .clk(clk), .we(OWre), .clr(reset));
  Multiplexer #(.width(16), .enable("false")) multiplexer_1 (
    .in0(multiplexer_2_out), .in1(jaddr), .out(multiplexer_1_out), .sel(J));
  Multiplexer #(.width(16), .enable("false")) multiplexer_2 (
    .in0(alu_2_result), .in1(alu_1_result), .out(multiplexer_2_out), .sel(and_1_out));
  and and_1 (and_1_out, multiplexer_3_out, BR);
  Multiplexer #(.enable("false")) multiplexer_3 (.in0(zero), .in1(neg), .out(multiplexer_3_out), .sel(Blt));
  Keyboard keyboard_1 (.clk(clk), .re(IRe), .clr(reset), .avail(keyboard_1_avail), .data(keyboard_1_data));
  alu alu_1 (
    .in_1(1'b0), .in_2(1'b0), .in_3(2'b00), .B(alu_2_result), .A(immd), .result(alu_1_result));  // open: ovf, zero, neg
  not not_1 (not_1_out, not_2_out);
  not not_2 (not_2_out, clk);
  assign bit_extender_1_out = {{9{1'b0}}, keyboard_1_data};  // Bit_Extender bit_extender_1
  \reg  reg_1 (.we(1'b1), .clk(not_1_out), .\input (multiplexer_1_out), .result(reg_1_result), .reset(reset));
  Multiplexer #(.width(16), .enable("false")) multiplexer_4 (
    .in0(16'h80), .in1(bit_extender_1_out), .out(keyin), .sel(keyboard_1_avail));
  ROM #(.addrWidth(16), .dataWidth(16)) rom_1 (.addr(reg_1_result), .data(reg_1_result));
  alu alu_2 (
    .in_1(1'b0), .in_2(1'b0), .in_3(2'b00), .B(reg_1_result), .A(16'h1), .result(alu_2_result));  // open: ovf, zero, neg
  Clock clock_1 (.out(clock_1_out));
  not not_3 (not_3_out, clock_1_out);
  not not_4 (clk, not_3_out);
  Multiplexer #(.width(16), .enable("false")) multiplexer_5 (
    .in0(multiplexer_11_out), .in1(alu_2_result), .out(multiplexer_5_out), .sel(JAL));
  BitSelector #(.width(16), .group(3)) bitselector_1 (.in(undriven), .out(amt), .sel(3'b000));
  BitSelector #(.width(16), .group(12)) bitselector_2 (.in(undriven), .out(bitselector_2_out), .sel(1'b0));
  BitSelector #(.width(16), .group(4)) bitselector_3 (.in(undriven), .out(bitselector_3_out), .sel(2'b11));
  control control_1 (
    .in_1(bitselector_3_out), .Rdst(Rdst), .ALUop(ALUop), .sub(sub), .ALUinB(ALUinB), .Shft(Shft),
    .RShft(RShft), .Rwe(Rwe), .DMwe(DMwe), .Rwd(Rwd), .BR(BR), .Blt(Blt), .J(J), .JAL(JAL), .OWre(OWre),
    .IRe(IRe));
  Multiplexer #(.width(16), .enable("false")) multiplexer_6 (
    .in0(multiplexer_5_out), .in1(keyin), .out(multiplexer_6_out), .sel(IRe));
  not not_5 (not_5_out, clk);
  assign jaddr = {{4{bitselector_2_out[11]}}, bitselector_2_out};  // Bit_Extender bit_extender_2
  RegisterFile registerfile_1 (
    .RDVAL(multiplexer_6_out), .clk(Rwe), .we(not_6_out), .RS2VAL(rt), .RS1VAL(registerfile_1_rs1val),
    .RD(multiplexer_7_out), .RS1(bitselector_4_out), .RS2(bitselector_5_out), .reset(reset));  // open: out_11, out_12, out_9, out_10, out_13, out_14, out_15, out_16
  not not_6 (not_6_out, not_7_out);
  not not_7 (not_7_out, not_5_out);
  BitSelector #(.width(16), .group(3)) bitselector_4 (.in(undriven), .out(bitselector_4_out), .sel(3'b011));
  Multiplexer #(.width(3), .enable("false")) multiplexer_7 (
    .in0(multiplexer_8_out), .in1(3'b111), .out(multiplexer_7_out), .sel(JAL));
  Multiplexer #(.width(3), .enable("false")) multiplexer_8 (
    .in0(bitselector_5_out), .in1(bitselector_6_out), .out(multiplexer_8_out), .sel(Rdst));
  BitSelector #(.width(16), .group(3)) bitselector_5 (.in(undriven), .out(bitselector_5_out), .sel(3'b010));
  BitSelector #(.width(16), .group(3)) bitselector_6 (.in(undriven), .out(bitselector_6_out), .sel(3'b001));
  BitSelector #(.width(16), .group(6)) bitselector_7 (.in(undriven), .out(bitselector_7_out), .sel(2'b00));
  assign immd = {{10{bitselector_7_out[5]}}, bitselector_7_out};  // Bit_Extender bit_extender_3
  BitSelector #(.width(16), .group(7)) bitselector_8 (.in(registerfile_1_rs1val), .out(ascii), .sel(2'b00));
  Multiplexer #(.width(16), .enable("false")) multiplexer_9 (
    .in0(rt), .in1(immd), .out(multiplexer_9_out), .sel(ALUinB));
  not not_8 (not_8_out, clk);
  Multiplexer #(.width(16), .enable("false")) multiplexer_10 (
    .in0(lshifter_1_result), .in1(rshifter_1_result), .out(shiftOut), .sel(RShft));
  lshifter lshifter_1 (.in_1(amt), .\input (registerfile_1_rs1val), .result(lshifter_1_result));
  not not_9 (not_9_out, not_8_out);
  Multiplexer #(.width(16), .enable("false")) multiplexer_11 (
    .in0(multiplexer_12_out), .in1(shiftOut), .out(multiplexer_11_out), .sel(Shft));
  rshifter rshifter_1 (.in_1(amt), .\input (registerfile_1_rs1val), .result(rshifter_1_result));
  memory_latch memory_latch_1 (
    .address(alu_3_result), .WE(DMwe), .clk(not_9_out), .data_in(rt),
    .address_latched(memory_latch_1_address_latched), .WE_latched(memory_latch_1_we_latched),
    .OE_latched(memory_latch_1_oe_latched), .data_in_latched(memory_latch_1_data_in_latched));
  alu alu_3 (
    .in_1(1'b0), .in_2(sub), .in_3(ALUop), .B(multiplexer_9_out), .A(registerfile_1_rs1val),
    .result(alu_3_result), .zero(zero), .neg(neg));  // open: ovf
  RAM #(.addrWidth(16), .dataWidth(16), .trigger("high"), .databus("bibus")) ram_1 (
    .addr(memory_latch_1_address_latched), .we(memory_latch_1_we_latched), .oe(memory_latch_1_oe_latched),
    .din(memory_latch_1_data_in_latched), .dout(ram_1_dout));
  Multiplexer #(.width(16), .enable("false")) multiplexer_12 (
    .in0(alu_3_result), .in1(ram_1_dout), .out(multiplexer_12_out), .sel(Rwd));

  // Notes on the sheet:
  //   contents of rom_1 (hex, n*v repeats v):
  //   6100 6903 f008 62a0 e400 693f 313b 203f
endmodule

module alu (
  input  in_1,
  input  in_2,
  input  [1:0] in_3,
  input  [15:0] B,
  input  [15:0] A,
  output ovf,
  output [15:0] result,
  output zero,
  output neg
);

  wire aluslice_1_cout, aluslice_2_cout, aluslice_3_cout, aluslice_4_cout, aluslice_5_cout, aluslice_6_cout,
       aluslice_7_cout, aluslice_8_cout, aluslice_9_cout, aluslice_10_cout, aluslice_11_cout,
       aluslice_12_cout, aluslice_13_cout, aluslice_14_cout, aluslice_15_cout, aluslice_16_cout, or_1_out;

  aluslice aluslice_1 (
    .sub(in_2), .a(A[7]), .b(B[7]), .Cout(aluslice_1_cout), .Q(result[7]), .Cin(aluslice_3_cout), .F(in_3));
  aluslice aluslice_2 (
    .sub(in_2), .a(A[15]), .b(B[15]), .Cout(aluslice_2_cout), .Q(neg), .Cin(aluslice_4_cout), .F(in_3));
  xor xor_1 (ovf, aluslice_2_cout, aluslice_4_cout);
  aluslice aluslice_3 (
    .sub(in_2), .a(A[6]), .b(B[6]), .Cout(aluslice_3_cout), .Q(result[6]), .Cin(aluslice_5_cout), .F(in_3));
  aluslice aluslice_4 (
    .sub(in_2), .a(A[14]), .b(B[14]), .Cout(aluslice_4_cout), .Q(result[14]), .Cin(aluslice_6_cout), .F(in_3));
  aluslice aluslice_5 (
    .sub(in_2), .a(A[5]), .b(B[5]), .Cout(aluslice_5_cout), .Q(result[5]), .Cin(aluslice_7_cout), .F(in_3));
  aluslice aluslice_6 (
    .sub(in_2), .a(A[13]), .b(B[13]), .Cout(aluslice_6_cout), .Q(result[13]), .Cin(aluslice_8_cout), .F(in_3));
  aluslice aluslice_7 (
    .sub(in_2), .a(A[4]), .b(B[4]), .Cout(aluslice_7_cout), .Q(result[4]), .Cin(aluslice_9_cout), .F(in_3));
  aluslice aluslice_8 (
    .sub(in_2), .a(A[12]), .b(B[12]), .Cout(aluslice_8_cout), .Q(result[12]), .Cin(aluslice_10_cout), .F(in_3));
  aluslice aluslice_9 (
    .sub(in_2), .a(A[3]), .b(B[3]), .Cout(aluslice_9_cout), .Q(result[3]), .Cin(aluslice_11_cout), .F(in_3));
  aluslice aluslice_10 (
    .sub(in_2), .a(A[11]), .b(B[11]), .Cout(aluslice_10_cout), .Q(result[11]), .Cin(aluslice_12_cout),
    .F(in_3));
  aluslice aluslice_11 (
    .sub(in_2), .a(A[2]), .b(B[2]), .Cout(aluslice_11_cout), .Q(result[2]), .Cin(aluslice_13_cout), .F(in_3));
  aluslice aluslice_12 (
    .sub(in_2), .a(A[10]), .b(B[10]), .Cout(aluslice_12_cout), .Q(result[10]), .Cin(aluslice_14_cout),
    .F(in_3));
  aluslice aluslice_13 (
    .sub(in_2), .a(A[1]), .b(B[1]), .Cout(aluslice_13_cout), .Q(result[1]), .Cin(aluslice_15_cout), .F(in_3));
  aluslice aluslice_14 (
    .sub(in_2), .a(A[9]), .b(B[9]), .Cout(aluslice_14_cout), .Q(result[9]), .Cin(aluslice_16_cout), .F(in_3));
  aluslice aluslice_15 (.sub(in_2), .a(A[0]), .b(B[0]), .Cout(aluslice_15_cout), .Q(result[0]), .Cin(in_1), .F(in_3));
  aluslice aluslice_16 (
    .sub(in_2), .a(A[8]), .b(B[8]), .Cout(aluslice_16_cout), .Q(result[8]), .Cin(aluslice_1_cout), .F(in_3));
  not not_1 (zero, or_1_out);
  or or_1 (or_1_out, result[0], result[1], result[2], result[3], result[4], result[5], result[6], result[7], result[8], result[9], result[10], result[11], result[12], result[13], result[14], neg);

  assign result[15] = neg;

  // Other names for the same wires on the sheet: cin = in_1; cont[1:0] = in_3; q0 = result[0]; q1 = result[1];
  //   q2 = result[2]; q3 = result[3]; q4 = result[4]; q5 = result[5]; q6 = result[6]; q7 = result[7]; q8 = result[8];
  //   q9 = result[9]; q10 = result[10]; q11 = result[11]; q12 = result[12]; q13 = result[13]; q14 = result[14];
  //   q15 = neg; sub = in_2
endmodule

module aluslice (
  input  sub,
  input  a,
  input  b,
  input  [1:0] F,
  input  Cin,
  output Q,
  output Cout
);

  wire and_1_out, not_1_out, not_2_out, onebitadder_1_sum, or_1_out, s, xor_1_out;

  or or_1 (or_1_out, a, b);
  and and_1 (and_1_out, a, b);
  Multiplexer multiplexer_1 (.in0(onebitadder_1_sum), .in1(not_1_out), .out(s), .sel(sub));  // open: en
  not not_1 (not_1_out, onebitadder_1_sum);
  onebitadder onebitadder_1 (.a(xor_1_out), .b(b), .Sum(onebitadder_1_sum), .Cin(Cin), .Cout(Cout));
  xor xor_1 (xor_1_out, a, sub);
  not not_2 (not_2_out, b);
  Multiplexer #(.select(2), .enable("false")) multiplexer_2 (
    .in0(s), .in1(not_2_out), .in2(or_1_out), .in3(and_1_out), .out(Q), .sel(F));
endmodule

module \reg  (
  input  reset,
  input  we,
  input  clk,
  input  [15:0] \input ,
  output [15:0] result
);

  wire enable;

  D_Flip_Flop d_ff_1 (.D(\input [0]), .clk(enable), .Q(result[0]), .reset(reset));  // open: Qn, preset
  D_Flip_Flop d_ff_2 (.D(\input [1]), .clk(enable), .Q(result[1]), .reset(reset));  // open: Qn, preset
  D_Flip_Flop d_ff_3 (.D(\input [2]), .clk(enable), .Q(result[2]), .reset(reset));  // open: Qn, preset
  D_Flip_Flop d_ff_4 (.D(\input [3]), .clk(enable), .Q(result[3]), .reset(reset));  // open: Qn, preset
  D_Flip_Flop d_ff_5 (.D(\input [4]), .clk(enable), .Q(result[4]), .reset(reset));  // open: Qn, preset
  D_Flip_Flop d_ff_6 (.D(\input [5]), .clk(enable), .Q(result[5]), .reset(reset));  // open: Qn, preset
  D_Flip_Flop d_ff_7 (.D(\input [6]), .clk(enable), .Q(result[6]), .reset(reset));  // open: Qn, preset
  D_Flip_Flop d_ff_8 (.D(\input [7]), .clk(enable), .Q(result[7]), .reset(reset));  // open: Qn, preset
  D_Flip_Flop d_ff_9 (.D(\input [8]), .clk(enable), .Q(result[8]), .reset(reset));  // open: Qn, preset
  D_Flip_Flop d_ff_10 (.D(\input [9]), .clk(enable), .Q(result[9]), .reset(reset));  // open: Qn, preset
  D_Flip_Flop d_ff_11 (.D(\input [10]), .clk(enable), .Q(result[10]), .reset(reset));  // open: Qn, preset
  D_Flip_Flop d_ff_12 (.D(\input [11]), .clk(enable), .Q(result[11]), .reset(reset));  // open: Qn, preset
  D_Flip_Flop d_ff_13 (.D(\input [12]), .clk(enable), .Q(result[12]), .reset(reset));  // open: Qn, preset
  D_Flip_Flop d_ff_14 (.D(\input [13]), .clk(enable), .Q(result[13]), .reset(reset));  // open: Qn, preset
  D_Flip_Flop d_ff_15 (.D(\input [14]), .clk(enable), .Q(result[14]), .reset(reset));  // open: Qn, preset
  D_Flip_Flop d_ff_16 (.D(\input [15]), .clk(enable), .Q(result[15]), .reset(reset));  // open: Qn, preset
  and and_1 (enable, we, clk);

  // Other names for the same wires on the sheet: d0 = \input [0]; d1 = \input [1]; d2 = \input [2]; d3 = \input [3];
  //   d4 = \input [4]; d5 = \input [5]; d6 = \input [6]; d7 = \input [7]; d8 = \input [8]; d9 = \input [9];
  //   d10 = \input [10]; d11 = \input [11]; d12 = \input [12]; d13 = \input [13]; d14 = \input [14];
  //   d15 = \input [15]; q0 = result[0]; q1 = result[1]; q2 = result[2]; q3 = result[3]; q4 = result[4];
  //   q5 = result[5]; q6 = result[6]; q7 = result[7]; q8 = result[8]; q9 = result[9]; q10 = result[10];
  //   q11 = result[11]; q12 = result[12]; q13 = result[13]; q14 = result[14]; q15 = result[15]
endmodule

// q0
module RegisterFile (
  input  [15:0] RDVAL,
  input  clk,
  input  we,
  input  [2:0] RD,
  input  reset,
  input  [2:0] RS2,
  input  [2:0] RS1,
  output [15:0] RS2VAL,
  output [15:0] out_9,
  output [15:0] out_10,
  output [15:0] out_11,
  output [15:0] out_12,
  output [15:0] out_13,
  output [15:0] out_14,
  output [15:0] out_15,
  output [15:0] out_16,
  output [15:0] RS1VAL
);

  wire decoder_1_out0, decoder_1_out1, decoder_1_out2, decoder_1_out3, decoder_1_out4, decoder_1_out5,
       decoder_1_out6, decoder_1_out7, decoder_2_out0, decoder_2_out1, decoder_2_out2, decoder_2_out3,
       decoder_2_out4, decoder_2_out5, decoder_2_out6, decoder_2_out7, decoder_3_out0, decoder_3_out1,
       decoder_3_out2, decoder_3_out3, decoder_3_out4, decoder_3_out5, decoder_3_out6, decoder_3_out7, l0,
       l1, l2, l3, l4, l5, l6, l7;

  and and_1 (l0, decoder_1_out0, we);
  and and_2 (l1, decoder_1_out1, we);
  \reg  reg_1 (.we(l0), .clk(clk), .\input ({16{1'b0}}), .result(out_9), .reset(reset));
  \reg  reg_2 (.we(l4), .clk(clk), .\input (RDVAL), .result(out_13), .reset(reset));
  Decoder #(.select(3), .enable("false")) decoder_1 (
    .out0(decoder_1_out0), .out1(decoder_1_out1), .out2(decoder_1_out2), .out3(decoder_1_out3),
    .out4(decoder_1_out4), .out5(decoder_1_out5), .out6(decoder_1_out6), .out7(decoder_1_out7), .sel(RD));
  and and_3 (l2, decoder_1_out2, we);
  and and_4 (l3, decoder_1_out3, we);
  // Probe on out_9
  // Probe on out_13
  and and_5 (l5, decoder_1_out5, we);
  and and_6 (l4, decoder_1_out4, we);
  and and_7 (l6, decoder_1_out6, we);
  \reg  reg_3 (.we(l1), .clk(clk), .\input (RDVAL), .result(out_10), .reset(reset));
  // Probe on out_10
  \reg  reg_4 (.we(l5), .clk(clk), .\input (RDVAL), .result(out_14), .reset(reset));
  // Probe on out_14
  and and_8 (l7, decoder_1_out7, we);
  \reg  reg_5 (.we(l2), .clk(clk), .\input (RDVAL), .result(out_11), .reset(reset));
  // Probe on out_11
  \reg  reg_6 (.we(l6), .clk(clk), .\input (RDVAL), .result(out_15), .reset(reset));
  // Probe on out_15
  \reg  reg_7 (.we(l3), .clk(clk), .\input (RDVAL), .result(out_12), .reset(reset));
  // Probe on out_12
  \reg  reg_8 (.we(l7), .clk(clk), .\input (RDVAL), .result(out_16), .reset(reset));
  // Probe on out_16
  assign RS2VAL = decoder_2_out4 ? out_13 : 16'bz;  // Controlled_Buffer controlled_buffer_1
  assign RS2VAL = decoder_2_out3 ? out_12 : 16'bz;  // Controlled_Buffer controlled_buffer_2
  assign RS2VAL = decoder_2_out2 ? out_11 : 16'bz;  // Controlled_Buffer controlled_buffer_3
  assign RS2VAL = decoder_2_out1 ? out_10 : 16'bz;  // Controlled_Buffer controlled_buffer_4
  assign RS2VAL = decoder_2_out0 ? out_9 : 16'bz;  // Controlled_Buffer controlled_buffer_5
  Decoder #(.select(3)) decoder_2 (
    .out0(decoder_2_out0), .out1(decoder_2_out1), .out2(decoder_2_out2), .out3(decoder_2_out3),
    .out4(decoder_2_out4), .out5(decoder_2_out5), .out6(decoder_2_out6), .out7(decoder_2_out7), .sel(RS2));  // open: en
  assign RS1VAL = decoder_3_out4 ? out_13 : 16'bz;  // Controlled_Buffer controlled_buffer_6
  assign RS1VAL = decoder_3_out3 ? out_12 : 16'bz;  // Controlled_Buffer controlled_buffer_7
  assign RS1VAL = decoder_3_out2 ? out_11 : 16'bz;  // Controlled_Buffer controlled_buffer_8
  assign RS1VAL = decoder_3_out1 ? out_10 : 16'bz;  // Controlled_Buffer controlled_buffer_9
  assign RS1VAL = decoder_3_out0 ? out_9 : 16'bz;  // Controlled_Buffer controlled_buffer_10
  Decoder #(.select(3)) decoder_3 (
    .out0(decoder_3_out0), .out1(decoder_3_out1), .out2(decoder_3_out2), .out3(decoder_3_out3),
    .out4(decoder_3_out4), .out5(decoder_3_out5), .out6(decoder_3_out6), .out7(decoder_3_out7), .sel(RS1));  // open: en
  assign RS2VAL = decoder_2_out7 ? out_16 : 16'bz;  // Controlled_Buffer controlled_buffer_11
  assign RS2VAL = decoder_2_out6 ? out_15 : 16'bz;  // Controlled_Buffer controlled_buffer_12
  assign RS2VAL = decoder_2_out5 ? out_14 : 16'bz;  // Controlled_Buffer controlled_buffer_13
  assign RS1VAL = decoder_3_out7 ? out_16 : 16'bz;  // Controlled_Buffer controlled_buffer_14
  assign RS1VAL = decoder_3_out6 ? out_15 : 16'bz;  // Controlled_Buffer controlled_buffer_15
  assign RS1VAL = decoder_3_out5 ? out_14 : 16'bz;  // Controlled_Buffer controlled_buffer_16

  // Other names for the same wires on the sheet: q0[15:0] = out_9; q1[15:0] = out_10; q2[15:0] = out_11;
  //   q3[15:0] = out_12; q4[15:0] = out_13; q5[15:0] = out_14; q6[15:0] = out_15; q7[15:0] = out_16
endmodule

module control (
  input  [3:0] in_1,
  output Rdst,
  output ALUinB,
  output sub,
  output BR,
  output IRe,
  output Rwe,
  output [1:0] ALUop,
  output RShft,
  output Blt,
  output Shft,
  output DMwe,
  output J,
  output JAL,
  output Rwd,
  output OWre
);

  wire add, addi, beq, j_t, \or , shl, sub_t, subi;

  Decoder #(.select(4), .enable("false")) decoder_1 (
    .out0(Rwd), .out1(DMwe), .out2(beq), .out3(Blt), .out4(\or ), .out5(ALUop[0]), .out6(addi), .out7(add),
    .out8(sub_t), .out9(subi), .out10(RShft), .out11(shl), .out12(j_t), .out13(JAL), .out14(OWre),
    .out15(IRe), .sel(in_1));
  or or_1 (Rwe, subi, Rwd, add, sub_t, addi, IRe, ALUop[0], \or , RShft, shl, JAL);
  or or_2 (ALUinB, subi, Rwd, DMwe, addi);
  or or_3 (Shft, RShft, shl);
  or or_4 (Rdst, shl, \or , ALUop[0], IRe, add, sub_t, RShft);
  or or_5 (ALUop[1], ALUop[0], \or );
  or or_6 (J, j_t, JAL);
  or or_7 (sub, sub_t, beq, Blt, subi);
  or or_8 (BR, beq, Blt);

  // Other names for the same wires on the sheet: and = ALUop[0]; input = IRe; lw = Rwd; output = OWre; shr = RShft;
  //   sw = DMwe
endmodule

module lshifter (
  input  [2:0] in_1,
  input  [15:0] \input ,
  output [15:0] result
);

  Multiplexer #(.select(3), .enable("false")) multiplexer_1 (
    .in0(\input [15]), .in1(\input [14]), .in2(\input [13]), .in3(\input [12]), .in4(\input [11]),
    .in5(\input [10]), .in6(\input [9]), .in7(\input [8]), .out(result[15]), .sel(in_1));
  Multiplexer #(.select(3), .enable("false")) multiplexer_2 (
    .in0(\input [11]), .in1(\input [10]), .in2(\input [9]), .in3(\input [8]), .in4(\input [7]),
    .in5(\input [6]), .in6(\input [5]), .in7(\input [4]), .out(result[11]), .sel(in_1));
  Multiplexer #(.select(3), .enable("false")) multiplexer_3 (
    .in0(\input [7]), .in1(\input [6]), .in2(\input [5]), .in3(\input [4]), .in4(\input [3]),
    .in5(\input [2]), .in6(\input [1]), .in7(\input [0]), .out(result[7]), .sel(in_1));
  Multiplexer #(.select(3), .enable("false")) multiplexer_4 (
    .in0(\input [3]), .in1(\input [2]), .in2(\input [1]), .in3(\input [0]), .in4(1'b0), .in5(1'b0),
    .in6(1'b0), .in7(1'b0), .out(result[3]), .sel(in_1));
  Multiplexer #(.select(3), .enable("false")) multiplexer_5 (
    .in0(\input [14]), .in1(\input [13]), .in2(\input [12]), .in3(\input [11]), .in4(\input [10]),
    .in5(\input [9]), .in6(\input [8]), .in7(\input [7]), .out(result[14]), .sel(in_1));
  Multiplexer #(.select(3), .enable("false")) multiplexer_6 (
    .in0(\input [10]), .in1(\input [9]), .in2(\input [8]), .in3(\input [7]), .in4(\input [6]),
    .in5(\input [5]), .in6(\input [4]), .in7(\input [3]), .out(result[10]), .sel(in_1));
  Multiplexer #(.select(3), .enable("false")) multiplexer_7 (
    .in0(\input [6]), .in1(\input [5]), .in2(\input [4]), .in3(\input [3]), .in4(\input [2]),
    .in5(\input [1]), .in6(\input [0]), .in7(1'b0), .out(result[6]), .sel(in_1));
  Multiplexer #(.select(3), .enable("false")) multiplexer_8 (
    .in0(\input [2]), .in1(\input [1]), .in2(\input [0]), .in3(1'b0), .in4(1'b0), .in5(1'b0), .in6(1'b0),
    .in7(1'b0), .out(result[2]), .sel(in_1));
  Multiplexer #(.select(3), .enable("false")) multiplexer_9 (
    .in0(\input [13]), .in1(\input [12]), .in2(\input [11]), .in3(\input [10]), .in4(\input [9]),
    .in5(\input [8]), .in6(\input [7]), .in7(\input [6]), .out(result[13]), .sel(in_1));
  Multiplexer #(.select(3), .enable("false")) multiplexer_10 (
    .in0(\input [9]), .in1(\input [8]), .in2(\input [7]), .in3(\input [6]), .in4(\input [5]),
    .in5(\input [4]), .in6(\input [3]), .in7(\input [2]), .out(result[9]), .sel(in_1));
  Multiplexer #(.select(3), .enable("false")) multiplexer_11 (
    .in0(\input [5]), .in1(\input [4]), .in2(\input [3]), .in3(\input [2]), .in4(\input [1]),
    .in5(\input [0]), .in6(1'b0), .in7(1'b0), .out(result[5]), .sel(in_1));
  Multiplexer #(.select(3), .enable("false")) multiplexer_12 (
    .in0(\input [1]), .in1(\input [0]), .in2(1'b0), .in3(1'b0), .in4(1'b0), .in5(1'b0), .in6(1'b0),
    .in7(1'b0), .out(result[1]), .sel(in_1));
  Multiplexer #(.select(3), .enable("false")) multiplexer_13 (
    .in0(\input [12]), .in1(\input [11]), .in2(\input [10]), .in3(\input [9]), .in4(\input [8]),
    .in5(\input [7]), .in6(\input [6]), .in7(\input [5]), .out(result[12]), .sel(in_1));
  Multiplexer #(.select(3), .enable("false")) multiplexer_14 (
    .in0(\input [8]), .in1(\input [7]), .in2(\input [6]), .in3(\input [5]), .in4(\input [4]),
    .in5(\input [3]), .in6(\input [2]), .in7(\input [1]), .out(result[8]), .sel(in_1));
  Multiplexer #(.select(3), .enable("false")) multiplexer_15 (
    .in0(\input [4]), .in1(\input [3]), .in2(\input [2]), .in3(\input [1]), .in4(\input [0]), .in5(1'b0),
    .in6(1'b0), .in7(1'b0), .out(result[4]), .sel(in_1));
  Multiplexer #(.select(3), .enable("false")) multiplexer_16 (
    .in0(\input [0]), .in1(1'b0), .in2(1'b0), .in3(1'b0), .in4(1'b0), .in5(1'b0), .in6(1'b0), .in7(1'b0),
    .out(result[0]), .sel(in_1));

  // Other names for the same wires on the sheet: i0 = \input [0]; i1 = \input [1]; i2 = \input [2]; i3 = \input [3];
  //   i4 = \input [4]; i5 = \input [5]; i6 = \input [6]; i7 = \input [7]; i8 = \input [8]; i9 = \input [9];
  //   i10 = \input [10]; i11 = \input [11]; i12 = \input [12]; i13 = \input [13]; i14 = \input [14];
  //   i15 = \input [15]; q0 = result[0]; q1 = result[1]; q2 = result[2]; q3 = result[3]; q4 = result[4];
  //   q5 = result[5]; q6 = result[6]; q7 = result[7]; q8 = result[8]; q9 = result[9]; q10 = result[10];
  //   q11 = result[11]; q12 = result[12]; q13 = result[13]; q14 = result[14]; q15 = result[15]; shft[2:0] = in_1
endmodule

module rshifter (
  input  [2:0] in_1,
  input  [15:0] \input ,
  output [15:0] result
);

  Multiplexer #(.select(3), .enable("false")) multiplexer_1 (
    .in0(\input [0]), .in1(\input [1]), .in2(\input [2]), .in3(\input [3]), .in4(\input [4]),
    .in5(\input [5]), .in6(\input [6]), .in7(\input [7]), .out(result[0]), .sel(in_1));
  Multiplexer #(.select(3), .enable("false")) multiplexer_2 (
    .in0(\input [4]), .in1(\input [5]), .in2(\input [6]), .in3(\input [7]), .in4(\input [8]),
    .in5(\input [9]), .in6(\input [10]), .in7(\input [11]), .out(result[4]), .sel(in_1));
  Multiplexer #(.select(3), .enable("false")) multiplexer_3 (
    .in0(\input [8]), .in1(\input [9]), .in2(\input [10]), .in3(\input [11]), .in4(\input [12]),
    .in5(\input [13]), .in6(\input [14]), .in7(\input [15]), .out(result[8]), .sel(in_1));
  Multiplexer #(.select(3), .enable("false")) multiplexer_4 (
    .in0(\input [12]), .in1(\input [13]), .in2(\input [14]), .in3(\input [15]), .in4(1'b0), .in5(1'b0),
    .in6(1'b0), .in7(1'b0), .out(result[12]), .sel(in_1));
  Multiplexer #(.select(3), .enable("false")) multiplexer_5 (
    .in0(\input [1]), .in1(\input [2]), .in2(\input [3]), .in3(\input [4]), .in4(\input [5]),
    .in5(\input [6]), .in6(\input [7]), .in7(\input [8]), .out(result[1]), .sel(in_1));
  Multiplexer #(.select(3), .enable("false")) multiplexer_6 (
    .in0(\input [5]), .in1(\input [6]), .in2(\input [7]), .in3(\input [8]), .in4(\input [9]),
    .in5(\input [10]), .in6(\input [11]), .in7(\input [12]), .out(result[5]), .sel(in_1));
  Multiplexer #(.select(3), .enable("false")) multiplexer_7 (
    .in0(\input [9]), .in1(\input [10]), .in2(\input [11]), .in3(\input [12]), .in4(\input [13]),
    .in5(\input [14]), .in6(\input [15]), .in7(1'b0), .out(result[9]), .sel(in_1));
  Multiplexer #(.select(3), .enable("false")) multiplexer_8 (
    .in0(\input [13]), .in1(\input [14]), .in2(\input [15]), .in3(1'b0), .in4(1'b0), .in5(1'b0), .in6(1'b0),
    .in7(1'b0), .out(result[13]), .sel(in_1));
  Multiplexer #(.select(3), .enable("false")) multiplexer_9 (
    .in0(\input [2]), .in1(\input [3]), .in2(\input [4]), .in3(\input [5]), .in4(\input [6]),
    .in5(\input [7]), .in6(\input [8]), .in7(\input [9]), .out(result[2]), .sel(in_1));
  Multiplexer #(.select(3), .enable("false")) multiplexer_10 (
    .in0(\input [6]), .in1(\input [7]), .in2(\input [8]), .in3(\input [9]), .in4(\input [10]),
    .in5(\input [11]), .in6(\input [12]), .in7(\input [12]), .out(result[6]), .sel(in_1));
  Multiplexer #(.select(3), .enable("false")) multiplexer_11 (
    .in0(\input [10]), .in1(\input [11]), .in2(\input [12]), .in3(\input [13]), .in4(\input [14]),
    .in5(\input [15]), .in6(1'b0), .in7(1'b0), .out(result[10]), .sel(in_1));
  Multiplexer #(.select(3), .enable("false")) multiplexer_12 (
    .in0(\input [14]), .in1(\input [15]), .in2(1'b0), .in3(1'b0), .in4(1'b0), .in5(1'b0), .in6(1'b0),
    .in7(1'b0), .out(result[14]), .sel(in_1));
  Multiplexer #(.select(3), .enable("false")) multiplexer_13 (
    .in0(\input [3]), .in1(\input [4]), .in2(\input [5]), .in3(\input [6]), .in4(\input [7]),
    .in5(\input [8]), .in6(\input [9]), .in7(\input [10]), .out(result[3]), .sel(in_1));
  Multiplexer #(.select(3), .enable("false")) multiplexer_14 (
    .in0(\input [7]), .in1(\input [8]), .in2(\input [9]), .in3(\input [10]), .in4(\input [11]),
    .in5(\input [12]), .in6(\input [13]), .in7(\input [14]), .out(result[7]), .sel(in_1));
  Multiplexer #(.select(3), .enable("false")) multiplexer_15 (
    .in0(\input [11]), .in1(\input [12]), .in2(\input [13]), .in3(\input [14]), .in4(\input [15]),
    .in5(1'b0), .in6(1'b0), .in7(1'b0), .out(result[11]), .sel(in_1));
  Multiplexer #(.select(3), .enable("false")) multiplexer_16 (
    .in0(\input [15]), .in1(1'b0), .in2(1'b0), .in3(1'b0), .in4(1'b0), .in5(1'b0), .in6(1'b0), .in7(1'b0),
    .out(result[15]), .sel(in_1));

  // Other names for the same wires on the sheet: i0 = \input [0]; i1 = \input [1]; i2 = \input [2]; i3 = \input [3];
  //   i4 = \input [4]; i5 = \input [5]; i6 = \input [6]; i7 = \input [7]; i8 = \input [8]; i9 = \input [9];
  //   i10 = \input [10]; i11 = \input [11]; i12 = \input [12]; i13 = \input [13]; i14 = \input [14];
  //   i15 = \input [15]; q0 = result[0]; q1 = result[1]; q2 = result[2]; q3 = result[3]; q4 = result[4];
  //   q5 = result[5]; q6 = result[6]; q7 = result[7]; q8 = result[8]; q9 = result[9]; q10 = result[10];
  //   q11 = result[11]; q12 = result[12]; q13 = result[13]; q14 = result[14]; q15 = result[15]; shft[2:0] = in_1
endmodule

module memory_latch (
  input  [15:0] address,
  input  WE,
  input  clk,
  input  [15:0] data_in,
  output [15:0] address_latched,
  output WE_latched,
  output OE_latched,
  output [15:0] data_in_latched
);

  wire d_ff_1_q;
  wire [15:0] register_1_q;

  Register #(.width(16), .trigger("falling")) register_1 (
    .D(address), .en(WE), .clk(clk), .Q(register_1_q));  // open: clr
  D_Flip_Flop #(.trigger("falling")) d_ff_1 (.D(WE), .clk(clk), .Q(d_ff_1_q));  // open: Qn, preset, reset
  Register #(.width(16), .trigger("falling")) register_2 (
    .D(data_in), .en(WE), .clk(clk), .Q(data_in_latched));  // open: clr
  Multiplexer #(.width(16), .enable("false")) multiplexer_1 (
    .in0(address), .in1(register_1_q), .out(address_latched), .sel(d_ff_1_q));
  and and_1 (WE_latched, clk, d_ff_1_q);
  not not_1 (OE_latched, WE_latched);
endmodule
